# Fritzing sketch HDT22WeatherStation (saved by Fritzing 0.9.4)
breadboards: 1

parts:
  Part1 = SparkFun ESP8266 Thing  # not connected
  Part2 = I2C level shifter bidirectional
  RHT1 = Humidity and Temperature Sensor RHT03

nets:
  N1: Part2.GND, RHT1.GND_1, RHT1.GND_2
  N2: Part2.HV1, RHT1.Data-signal
  N3: Part2.HV, RHT1.Vcc
